// Digital circuit pb170.dig as structural Verilog
module pb170 (
  input  A0,
  input  A1,
  input  A2,
  input  A3,
  input  B0,
  input  B1,
  input  B2,
  input  B3,
  input  OP_BIT_0,
  input  OP_BIT_1,
  output Y0,
  output Y1,
  output Y2,
  output Y3,
  output ZERO,
  output NEGATIVE,
  output OVERFLOW,
  output OP0,
  output OP1
);

  wire add_1_c_o, add_1_s, add_2_c_o, add_2_s, add_3_c_o, add_3_s, add_4_c_o, add_4_s, and_1_out, and_2_out,
       and_3_out, and_4_out, multiplexer_1_out, multiplexer_2_out, multiplexer_3_out, multiplexer_4_out,
       nand_1_out, nand_2_out, or_1_out, or_2_out, or_3_out, or_4_out, xor_1_out, xor_2_out, xor_3_out,
       xor_4_out, xor_5_out;

  xor xor_1 (xor_1_out, B0, OP_BIT_0);
  xor xor_2 (xor_2_out, B1, OP_BIT_0);
  xor xor_3 (xor_3_out, B2, OP_BIT_0);
  xor xor_4 (xor_4_out, B3, OP_BIT_0);
  and and_1 (and_1_out, A0, B0);
  and and_2 (and_2_out, A1, B1);
  and and_3 (and_3_out, A2, B2);
  and and_4 (and_4_out, A3, B3);
  or or_1 (or_1_out, A0, B0);
  or or_2 (or_2_out, A1, B1);
  or or_3 (or_3_out, A2, B2);
  or or_4 (or_4_out, A3, B3);
  Add add_1 (.a(A0), .b(xor_1_out), .c_i(OP_BIT_0), .s(add_1_s), .c_o(add_1_c_o));
  Add add_2 (.a(A1), .b(xor_2_out), .c_i(add_1_c_o), .s(add_2_s), .c_o(add_2_c_o));
  Add add_3 (.a(A2), .b(xor_3_out), .c_i(add_2_c_o), .s(add_3_s), .c_o(add_3_c_o));
  Add add_4 (.a(A3), .b(xor_4_out), .c_i(add_3_c_o), .s(add_4_s), .c_o(add_4_c_o));
  nand nand_1 (nand_1_out, OP_BIT_1, OP_BIT_1);
  Multiplexer multiplexer_1 (.sel(OP_BIT_0), .in_0(and_1_out), .in_1(or_1_out), .out(multiplexer_1_out));
  Multiplexer multiplexer_2 (.sel(OP_BIT_0), .in_0(and_2_out), .in_1(or_2_out), .out(multiplexer_2_out));
  Multiplexer multiplexer_3 (.sel(OP_BIT_0), .in_0(and_3_out), .in_1(or_3_out), .out(multiplexer_3_out));
  Multiplexer multiplexer_4 (.sel(OP_BIT_0), .in_0(and_4_out), .in_1(or_4_out), .out(multiplexer_4_out));
  xor xor_5 (xor_5_out, add_4_c_o, add_3_c_o);
  nand nand_2 (nand_2_out, xor_5_out, nand_1_out);
  Multiplexer multiplexer_5 (.sel(OP_BIT_1), .in_0(add_1_s), .in_1(multiplexer_1_out), .out(Y0));
  Multiplexer multiplexer_6 (.sel(OP_BIT_1), .in_0(add_2_s), .in_1(multiplexer_2_out), .out(Y1));
  Multiplexer multiplexer_7 (.sel(OP_BIT_1), .in_0(add_3_s), .in_1(multiplexer_3_out), .out(Y2));
  Multiplexer multiplexer_8 (.sel(OP_BIT_1), .in_0(add_4_s), .in_1(multiplexer_4_out), .out(NEGATIVE));
  xor xor_6 (OVERFLOW, 1'b1, nand_2_out);
  nor nor_1 (ZERO, NEGATIVE, Y2, Y1, Y0);

  assign OP0 = OP_BIT_0;
  assign OP1 = OP_BIT_1;
  assign Y3 = NEGATIVE;
endmodule

/* Test case Addition:
OP_BIT_1 OP_BIT_0 A3 A2 A1 A0 B3 B2 B1 B0 Y3 Y2 Y1 Y0 OVERFLOW ZERO NEGATIVE
0        0        0  0  0  0  0  0  0  0  0  0  0  0  0        1    0       
0        0        0  0  0  1  0  0  0  0  0  0  0  1  0        0    0       
0        0        0  0  1  0  0  0  0  0  0  0  1  0  0        0    0       
0        0        0  0  1  1  0  0  0  0  0  0  1  1  0        0    0       
0        0        0  1  0  0  0  0  0  0  0  1  0  0  0        0    0       
0        0        0  1  0  1  0  0  0  0  0  1  0  1  0        0    0       
0        0        0  1  1  0  0  0  0  0  0  1  1  0  0        0    0       
0        0        0  1  1  1  0  0  0  0  0  1  1  1  0        0    0       
0        0        1  0  0  0  0  0  0  0  1  0  0  0  0        0    1       
0        0        1  0  0  1  0  0  0  0  1  0  0  1  0        0    1       
0        0        1  0  1  0  0  0  0  0  1  0  1  0  0        0    1       
0        0        1  0  1  1  0  0  0  0  1  0  1  1  0        0    1       
0        0        1  1  0  0  0  0  0  0  1  1  0  0  0        0    1       
0        0        1  1  0  1  0  0  0  0  1  1  0  1  0        0    1       
0        0        1  1  1  0  0  0  0  0  1  1  1  0  0        0    1       
0        0        1  1  1  1  0  0  0  0  1  1  1  1  0        0    1       
0        0        0  0  0  0  0  0  0  1  0  0  0  1  0        0    0       
0        0        0  0  0  1  0  0  0  1  0  0  1  0  0        0    0       
0        0        0  0  1  0  0  0  0  1  0  0  1  1  0        0    0       
0        0        0  0  1  1  0  0  0  1  0  1  0  0  0        0    0       
0        0        0  1  0  0  0  0  0  1  0  1  0  1  0        0    0       
0        0        0  1  0  1  0  0  0  1  0  1  1  0  0        0    0       
0        0        0  1  1  0  0  0  0  1  0  1  1  1  0        0    0       
0        0        0  1  1  1  0  0  0  1  1  0  0  0  1        0    1       
0        0        1  0  0  0  0  0  0  1  1  0  0  1  0        0    1       
0        0        1  0  0  1  0  0  0  1  1  0  1  0  0        0    1       
0        0        1  0  1  0  0  0  0  1  1  0  1  1  0        0    1       
0        0        1  0  1  1  0  0  0  1  1  1  0  0  0        0    1       
0        0        1  1  0  0  0  0  0  1  1  1  0  1  0        0    1       
0        0        1  1  0  1  0  0  0  1  1  1  1  0  0        0    1       
0        0        1  1  1  0  0  0  0  1  1  1  1  1  0        0    1       
0        0        1  1  1  1  0  0  0  1  0  0  0  0  0        1    0       
0        0        0  0  0  0  0  0  1  0  0  0  1  0  0        0    0       
0        0        0  0  0  1  0  0  1  0  0  0  1  1  0        0    0       
0        0        0  0  1  0  0  0  1  0  0  1  0  0  0        0    0       
0        0        0  0  1  1  0  0  1  0  0  1  0  1  0        0    0       
0        0        0  1  0  0  0  0  1  0  0  1  1  0  0        0    0       
0        0        0  1  0  1  0  0  1  0  0  1  1  1  0        0    0       
0        0        0  1  1  0  0  0  1  0  1  0  0  0  1        0    1       
0        0        0  1  1  1  0  0  1  0  1  0  0  1  1        0    1       
0        0        1  0  0  0  0  0  1  0  1  0  1  0  0        0    1       
0        0        1  0  0  1  0  0  1  0  1  0  1  1  0        0    1       
0        0        1  0  1  0  0  0  1  0  1  1  0  0  0        0    1       
0        0        1  0  1  1  0  0  1  0  1  1  0  1  0        0    1       
0        0        1  1  0  0  0  0  1  0  1  1  1  0  0        0    1       
0        0        1  1  0  1  0  0  1  0  1  1  1  1  0        0    1       
0        0        1  1  1  0  0  0  1  0  0  0  0  0  0        1    0       
0        0        1  1  1  1  0  0  1  0  0  0  0  1  0        0    0       
0        0        0  0  0  0  0  0  1  1  0  0  1  1  0        0    0       
0        0        0  0  0  1  0  0  1  1  0  1  0  0  0        0    0       
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*/

/* Test case Subtraction:
OP_BIT_1 OP_BIT_0 A3 A2 A1 A0 B3 B2 B1 B0 Y3 Y2 Y1 Y0 OVERFLOW ZERO NEGATIVE
0        1        0  0  0  0  0  0  0  0  0  0  0  0  0        1    0       
0        1        0  0  0  1  0  0  0  0  0  0  0  1  0        0    0       
0        1        0  0  1  0  0  0  0  0  0  0  1  0  0        0    0       
0        1        0  0  1  1  0  0  0  0  0  0  1  1  0        0    0       
0        1        0  1  0  0  0  0  0  0  0  1  0  0  0        0    0       
0        1        0  1  0  1  0  0  0  0  0  1  0  1  0        0    0       
0        1        0  1  1  0  0  0  0  0  0  1  1  0  0        0    0       
0        1        0  1  1  1  0  0  0  0  0  1  1  1  0        0    0       
0        1        1  0  0  0  0  0  0  0  1  0  0  0  0        0    1       
0        1        1  0  0  1  0  0  0  0  1  0  0  1  0        0    1       
0        1        1  0  1  0  0  0  0  0  1  0  1  0  0        0    1       
0        1        1  0  1  1  0  0  0  0  1  0  1  1  0        0    1       
0        1        1  1  0  0  0  0  0  0  1  1  0  0  0        0    1       
0        1        1  1  0  1  0  0  0  0  1  1  0  1  0        0    1       
0        1        1  1  1  0  0  0  0  0  1  1  1  0  0        0    1       
0        1        1  1  1  1  0  0  0  0  1  1  1  1  0        0    1       
0        1        0  0  0  0  0  0  0  1  1  1  1  1  0        0    1       
0        1        0  0  0  1  0  0  0  1  0  0  0  0  0        1    0       
0        1        0  0  1  0  0  0  0  1  0  0  0  1  0        0    0       
0        1        0  0  1  1  0  0  0  1  0  0  1  0  0        0    0       
0        1        0  1  0  0  0  0  0  1  0  0  1  1  0        0    0       
0        1        0  1  0  1  0  0  0  1  0  1  0  0  0        0    0       
0        1        0  1  1  0  0  0  0  1  0  1  0  1  0        0    0       
0        1        0  1  1  1  0  0  0  1  0  1  1  0  0        0    0       
0        1        1  0  0  0  0  0  0  1  0  1  1  1  1        0    0       
0        1        1  0  0  1  0  0  0  1  1  0  0  0  0        0    1       
0        1        1  0  1  0  0  0  0  1  1  0  0  1  0        0    1       
0        1        1  0  1  1  0  0  0  1  1  0  1  0  0        0    1       
0        1        1  1  0  0  0  0  0  1  1  0  1  1  0        0    1       
0        1        1  1  0  1  0  0  0  1  1  1  0  0  0        0    1       
0        1        1  1  1  0  0  0  0  1  1  1  0  1  0        0    1       
0        1        1  1  1  1  0  0  0  1  1  1  1  0  0        0    1       
0        1        0  0  0  0  0  0  1  0  1  1  1  0  0        0    1       
0        1        0  0  0  1  0  0  1  0  1  1  1  1  0        0    1       
0        1        0  0  1  0  0  0  1  0  0  0  0  0  0        1    0       
0        1        0  0  1  1  0  0  1  0  0  0  0  1  0        0    0       
0        1        0  1  0  0  0  0  1  0  0  0  1  0  0        0    0       
0        1        0  1  0  1  0  0  1  0  0  0  1  1  0        0    0       
0        1        0  1  1  0  0  0  1  0  0  1  0  0  0        0    0       
0        1        0  1  1  1  0  0  1  0  0  1  0  1  0        0    0       
0        1        1  0  0  0  0  0  1  0  0  1  1  0  1        0    0       
0        1        1  0  0  1  0  0  1  0  0  1  1  1  1        0    0       
0        1        1  0  1  0  0  0  1  0  1  0  0  0  0        0    1       
0        1        1  0  1  1  0  0  1  0  1  0  0  1  0        0    1       
0        1        1  1  0  0  0  0  1  0  1  0  1  0  0        0    1       
0        1        1  1  0  1  0  0  1  0  1  0  1  1  0        0    1       
0        1        1  1  1  0  0  0  1  0  1  1  0  0  0        0    1       
0        1        1  1  1  1  0  0  1  0  1  1  0  1  0        0    1       
0        1        0  0  0  0  0  0  1  1  1  1  0  1  0        0    1       
0        1        0  0  0  1  0  0  1  1  1  1  1  0  0        0    1       
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*/

/* Test case Logic AND:
OP_BIT_1 OP_BIT_0 A3 A2 A1 A0 B3 B2 B1 B0 Y3 Y2 Y1 Y0 OVERFLOW ZERO NEGATIVE
1        0        0  0  0  0  0  0  0  0  0  0  0  0  0        1    0       
1        0        0  0  0  1  0  0  0  0  0  0  0  0  0        1    0       
1        0        0  0  1  0  0  0  0  0  0  0  0  0  0        1    0       
1        0        0  0  1  1  0  0  0  0  0  0  0  0  0        1    0       
1        0        0  1  0  0  0  0  0  0  0  0  0  0  0        1    0       
1        0        0  1  0  1  0  0  0  0  0  0  0  0  0        1    0       
1        0        0  1  1  0  0  0  0  0  0  0  0  0  0        1    0       
1        0        0  1  1  1  0  0  0  0  0  0  0  0  0        1    0       
1        0        1  0  0  0  0  0  0  0  0  0  0  0  0        1    0       
1        0        1  0  0  1  0  0  0  0  0  0  0  0  0        1    0       
1        0        1  0  1  0  0  0  0  0  0  0  0  0  0        1    0       
1        0        1  0  1  1  0  0  0  0  0  0  0  0  0        1    0       
1        0        1  1  0  0  0  0  0  0  0  0  0  0  0        1    0       
1        0        1  1  0  1  0  0  0  0  0  0  0  0  0        1    0       
1        0        1  1  1  0  0  0  0  0  0  0  0  0  0        1    0       
1        0        1  1  1  1  0  0  0  0  0  0  0  0  0        1    0       
1        0        0  0  0  0  0  0  0  1  0  0  0  0  0        1    0       
1        0        0  0  0  1  0  0  0  1  0  0  0  1  0        0    0       
1        0        0  0  1  0  0  0  0  1  0  0  0  0  0        1    0       
1        0        0  0  1  1  0  0  0  1  0  0  0  1  0        0    0       
1        0        0  1  0  0  0  0  0  1  0  0  0  0  0        1    0       
1        0        0  1  0  1  0  0  0  1  0  0  0  1  0        0    0       
1        0        0  1  1  0  0  0  0  1  0  0  0  0  0        1    0       
1        0        0  1  1  1  0  0  0  1  0  0  0  1  0        0    0       
1        0        1  0  0  0  0  0  0  1  0  0  0  0  0        1    0       
1        0        1  0  0  1  0  0  0  1  0  0  0  1  0        0    0       
1        0        1  0  1  0  0  0  0  1  0  0  0  0  0        1    0       
1        0        1  0  1  1  0  0  0  1  0  0  0  1  0        0    0       
1        0        1  1  0  0  0  0  0  1  0  0  0  0  0        1    0       
1        0        1  1  0  1  0  0  0  1  0  0  0  1  0        0    0       
1        0        1  1  1  0  0  0  0  1  0  0  0  0  0        1    0       
1        0        1  1  1  1  0  0  0  1  0  0  0  1  0        0    0       
1        0        0  0  0  0  0  0  1  0  0  0  0  0  0        1    0       
1        0        0  0  0  1  0  0  1  0  0  0  0  0  0        1    0       
1        0        0  0  1  0  0  0  1  0  0  0  1  0  0        0    0       
1        0        0  0  1  1  0  0  1  0  0  0  1  0  0        0    0       
1        0        0  1  0  0  0  0  1  0  0  0  0  0  0        1    0       
1        0        0  1  0  1  0  0  1  0  0  0  0  0  0        1    0       
1        0        0  1  1  0  0  0  1  0  0  0  1  0  0        0    0       
1        0        0  1  1  1  0  0  1  0  0  0  1  0  0        0    0       
1        0        1  0  0  0  0  0  1  0  0  0  0  0  0        1    0       
1        0        1  0  0  1  0  0  1  0  0  0  0  0  0        1    0       
1        0        1  0  1  0  0  0  1  0  0  0  1  0  0        0    0       
1        0        1  0  1  1  0  0  1  0  0  0  1  0  0        0    0       
1        0        1  1  0  0  0  0  1  0  0  0  0  0  0        1    0       
1        0        1  1  0  1  0  0  1  0  0  0  0  0  0        1    0       
1        0        1  1  1  0  0  0  1  0  0  0  1  0  0        0    0       
1        0        1  1  1  1  0  0  1  0  0  0  1  0  0        0    0       
1        0        0  0  0  0  0  0  1  1  0  0  0  0  0        1    0       
1        0        0  0  0  1  0  0  1  1  0  0  0  1  0        0    0       
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*/

/* Test case Logic OR:
OP_BIT_1 OP_BIT_0 A3 A2 A1 A0 B3 B2 B1 B0 Y3 Y2 Y1 Y0 OVERFLOW ZERO NEGATIVE
1        1        0  0  0  0  0  0  0  0  0  0  0  0  0        1    0       
1        1        0  0  0  1  0  0  0  0  0  0  0  1  0        0    0       
1        1        0  0  1  0  0  0  0  0  0  0  1  0  0        0    0       
1        1        0  0  1  1  0  0  0  0  0  0  1  1  0        0    0       
1        1        0  1  0  0  0  0  0  0  0  1  0  0  0        0    0       
1        1        0  1  0  1  0  0  0  0  0  1  0  1  0        0    0       
1        1        0  1  1  0  0  0  0  0  0  1  1  0  0        0    0       
1        1        0  1  1  1  0  0  0  0  0  1  1  1  0        0    0       
1        1        1  0  0  0  0  0  0  0  1  0  0  0  0        0    1       
1        1        1  0  0  1  0  0  0  0  1  0  0  1  0        0    1       
1        1        1  0  1  0  0  0  0  0  1  0  1  0  0        0    1       
1        1        1  0  1  1  0  0  0  0  1  0  1  1  0        0    1       
1        1        1  1  0  0  0  0  0  0  1  1  0  0  0        0    1       
1        1        1  1  0  1  0  0  0  0  1  1  0  1  0        0    1       
1        1        1  1  1  0  0  0  0  0  1  1  1  0  0        0    1       
1        1        1  1  1  1  0  0  0  0  1  1  1  1  0        0    1       
1        1        0  0  0  0  0  0  0  1  0  0  0  1  0        0    0       
1        1        0  0  0  1  0  0  0  1  0  0  0  1  0        0    0       
1        1        0  0  1  0  0  0  0  1  0  0  1  1  0        0    0       
1        1        0  0  1  1  0  0  0  1  0  0  1  1  0        0    0       
1        1        0  1  0  0  0  0  0  1  0  1  0  1  0        0    0       
1        1        0  1  0  1  0  0  0  1  0  1  0  1  0        0    0       
1        1        0  1  1  0  0  0  0  1  0  1  1  1  0        0    0       
1        1        0  1  1  1  0  0  0  1  0  1  1  1  0        0    0       
1        1        1  0  0  0  0  0  0  1  1  0  0  1  0        0    1       
1        1        1  0  0  1  0  0  0  1  1  0  0  1  0        0    1       
1        1        1  0  1  0  0  0  0  1  1  0  1  1  0        0    1       
1        1        1  0  1  1  0  0  0  1  1  0  1  1  0        0    1       
1        1        1  1  0  0  0  0  0  1  1  1  0  1  0        0    1       
1        1        1  1  0  1  0  0  0  1  1  1  0  1  0        0    1       
1        1        1  1  1  0  0  0  0  1  1  1  1  1  0        0    1       
1        1        1  1  1  1  0  0  0  1  1  1  1  1  0        0    1       
1        1        0  0  0  0  0  0  1  0  0  0  1  0  0        0    0       
1        1        0  0  0  1  0  0  1  0  0  0  1  1  0        0    0       
1        1        0  0  1  0  0  0  1  0  0  0  1  0  0        0    0       
1        1        0  0  1  1  0  0  1  0  0  0  1  1  0        0    0       
1        1        0  1  0  0  0  0  1  0  0  1  1  0  0        0    0       
1        1        0  1  0  1  0  0  1  0  0  1  1  1  0        0    0       
1        1        0  1  1  0  0  0  1  0  0  1  1  0  0        0    0       
1        1        0  1  1  1  0  0  1  0  0  1  1  1  0        0    0       
1        1        1  0  0  0  0  0  1  0  1  0  1  0  0        0    1       
1        1        1  0  0  1  0  0  1  0  1  0  1  1  0        0    1       
1        1        1  0  1  0  0  0  1  0  1  0  1  0  0        0    1       
1        1        1  0  1  1  0  0  1  0  1  0  1  1  0        0    1       
1        1        1  1  0  0  0  0  1  0  1  1  1  0  0        0    1       
1        1        1  1  0  1  0  0  1  0  1  1  1  1  0        0    1       
1        1        1  1  1  0  0  0  1  0  1  1  1  0  0        0    1       
1        1        1  1  1  1  0  0  1  0  1  1  1  1  0        0    1       
1        1        0  0  0  0  0  0  1  1  0  0  1  1  0        0    0       
1        1        0  0  0  1  0  0  1  1  0  0  1  1  0        0    0       
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*/
